// Digital circuit bin2hex.dig as structural Verilog
module bin2hex (
  input  in_1,
  input  in_2,
  input  in_3,
  input  in_4
);

  Seven_Seg_Hex seven_seg_hex_1 (.d({in_4, in_3, in_2, in_1}), .dp(1'b0));
endmodule
