// Digital circuit emirasal_hw1.dig as structural Verilog
module emirasal_hw1 (
  input  in_1,
  input  in_2,
  input  in_3,
  input  in_4,
  input  in_5,
  input  in_6
);

  wire [3:0] add_1_s;

  Seven_Seg_Hex seven_seg_hex_1 (.d(add_1_s), .dp(1'b0));
  Add #(.Bits(3)) add_1 (
    .a({in_3, in_2, in_1}), .b({in_6, in_5, in_4}), .c_i(1'b0), .s(add_1_s[2:0]), .c_o(add_1_s[3]));
endmodule
