// Digital circuit emirasal_hw2.dig as structural Verilog
module emirasal_hw2 (
  input  in_1,
  input  in_2
);

  wire and_1_out, not_1_out, not_2_out, or_1_out, or_2_out, or_3_out, or_4_out;

  not not_1 (not_1_out, in_1);
  not not_2 (not_2_out, in_2);
  or or_1 (or_1_out, not_2_out, in_1);
  or or_2 (or_2_out, not_2_out, in_2);
  or or_3 (or_3_out, in_2, not_1_out);
  or or_4 (or_4_out, not_2_out, in_1);
  and and_1 (and_1_out, not_2_out, not_1_out);
  Seven_Seg seven_seg_1 (
    .a(or_1_out), .b(or_2_out), .c(or_3_out), .d(or_4_out), .e(not_2_out), .f(and_1_out), .g(in_1), .dp(1'b0));
endmodule
