// Digital circuit lab2.dig as structural Verilog
module lab2 (
  input  D1,
  input  D0,
  output G,
  output F,
  output E,
  output D,
  output C,
  output B,
  output A,
  output [7:0] AN
);

  wire not_1_out, not_2_out;

  not not_1 (not_1_out, D1);
  not not_2 (not_2_out, D0);
  nor nor_1 (G, D0, D1);
  nand nand_1 (F, D0, D1);
  or or_1 (E, not_2_out, D1);
  xnor xnor_1 (D, D0, D1);
  and and_1 (C, not_1_out, D0);
  xnor xnor_2 (A, D0, D1);

  assign AN = 8'hfe;
  assign B = 1'b0;
endmodule
