// Digital circuit lab2_test.dig as structural Verilog
module lab2_test (
);

  wire dipswitch_1_out, dipswitch_2_out, lab2_1_a, lab2_1_b, lab2_1_c, lab2_1_d, lab2_1_e, lab2_1_f,
       lab2_1_g, not_1_out, not_2_out, not_3_out, not_4_out, not_5_out, not_6_out, not_7_out;

  DipSwitch dipswitch_1 (.out(dipswitch_1_out));
  DipSwitch dipswitch_2 (.out(dipswitch_2_out));
  lab2 lab2_1 (
    .D1(dipswitch_1_out), .D0(dipswitch_2_out), .G(lab2_1_g), .F(lab2_1_f), .E(lab2_1_e), .D(lab2_1_d),
    .C(lab2_1_c), .B(lab2_1_b), .A(lab2_1_a));  // open: AN
  not not_1 (not_1_out, lab2_1_g);
  not not_2 (not_2_out, lab2_1_f);
  not not_3 (not_3_out, lab2_1_e);
  not not_4 (not_4_out, lab2_1_d);
  not not_5 (not_5_out, lab2_1_c);
  not not_6 (not_6_out, lab2_1_b);
  not not_7 (not_7_out, lab2_1_a);
  Seven_Seg seven_seg_1 (
    .a(not_7_out), .b(not_6_out), .c(not_5_out), .d(not_4_out), .e(not_3_out), .f(not_2_out), .g(not_1_out),
    .dp(1'b0));
endmodule
