// Digital circuit lab3.dig as structural Verilog
module lab3 (
  input  C,
  input  B,
  input  A,
  output F
);

  wire and_1_out, and_2_out, and_3_out, and_4_out, not_1_out, not_2_out, not_3_out;

  not not_1 (not_1_out, C);
  not not_2 (not_2_out, B);
  not not_3 (not_3_out, A);
  and and_1 (and_1_out, A, not_2_out, not_1_out);
  and and_2 (and_2_out, not_3_out, not_2_out, C);
  and and_3 (and_3_out, A, B, C);
  and and_4 (and_4_out, not_3_out, B, not_1_out);
  or or_1 (F, and_1_out, and_2_out, and_3_out, and_4_out);
endmodule
