// Digital circuit counter4test.dig as structural Verilog
module counter4test (
  input  clk
);

  wire counterbcdseven_1_a, counterbcdseven_1_b, counterbcdseven_1_c, counterbcdseven_1_d,
       counterbcdseven_1_e, counterbcdseven_1_f, counterbcdseven_1_g, not_1_out, not_2_out, not_3_out,
       not_4_out, not_5_out, not_6_out, not_7_out;

  counterBCDseven counterbcdseven_1 (
    .CLK(clk), .A(counterbcdseven_1_a), .B(counterbcdseven_1_b), .C(counterbcdseven_1_c),
    .D(counterbcdseven_1_d), .E(counterbcdseven_1_e), .F(counterbcdseven_1_f), .G(counterbcdseven_1_g));  // open: AN
  not not_1 (not_1_out, counterbcdseven_1_a);
  not not_2 (not_2_out, counterbcdseven_1_b);
  not not_3 (not_3_out, counterbcdseven_1_c);
  not not_4 (not_4_out, counterbcdseven_1_d);
  not not_5 (not_5_out, counterbcdseven_1_e);
  not not_6 (not_6_out, counterbcdseven_1_f);
  not not_7 (not_7_out, counterbcdseven_1_g);
  Seven_Seg seven_seg_1 (
    .a(not_1_out), .b(not_2_out), .c(not_3_out), .d(not_4_out), .e(not_5_out), .f(not_6_out), .g(not_7_out),
    .dp(1'b0));
endmodule
