// Digital circuit counterBCDseven.dig as structural Verilog
module counterBCDseven (
  input  CLK,
  output A,
  output B,
  output C,
  output D,
  output E,
  output F,
  output G,
  output [7:0] AN
);

  wire and_1_out, and_2_out, and_3_out, and_4_out, and_5_out, and_6_out, comparator_1_eq, d_ff_1_nq,
       d_ff_2_nq, d_ff_3_nq, d_ff_4_nq, multiplexer_1_out, multiplexer_2_out, multiplexer_3_out, not_1_out;
  wire [3:0] d_ff_1_q;

  not not_1 (not_1_out, comparator_1_eq);
  and and_1 (and_1_out, d_ff_1_nq, not_1_out);
  and and_2 (and_2_out, multiplexer_1_out, not_1_out);
  and and_3 (and_3_out, multiplexer_2_out, not_1_out);
  and and_4 (and_4_out, multiplexer_3_out, not_1_out);
  D_FF d_ff_1 (.D(and_1_out), .C(CLK), .Q(d_ff_1_q[0]), .nQ(d_ff_1_nq));
  D_FF d_ff_2 (.D(and_2_out), .C(CLK), .Q(d_ff_1_q[1]), .nQ(d_ff_2_nq));
  D_FF d_ff_3 (.D(and_3_out), .C(CLK), .Q(d_ff_1_q[2]), .nQ(d_ff_3_nq));
  D_FF d_ff_4 (.D(and_4_out), .C(CLK), .Q(d_ff_1_q[3]), .nQ(d_ff_4_nq));
  Multiplexer multiplexer_1 (.sel(d_ff_1_q[0]), .in_0(d_ff_1_q[1]), .in_1(d_ff_2_nq), .out(multiplexer_1_out));
  Multiplexer multiplexer_2 (.sel(and_5_out), .in_0(d_ff_1_q[2]), .in_1(d_ff_3_nq), .out(multiplexer_2_out));
  Multiplexer multiplexer_3 (.sel(and_6_out), .in_0(d_ff_1_q[3]), .in_1(d_ff_4_nq), .out(multiplexer_3_out));
  and and_5 (and_5_out, d_ff_1_q[0], d_ff_1_q[1]);
  and and_6 (and_6_out, d_ff_1_q[2], and_5_out);
  Comparator #(.Bits(4)) comparator_1 (.a(d_ff_1_q), .b(4'b0011), .eq(comparator_1_eq));  // open: gt, lt
  bin2seven #(.applicationType("IVERILOG")) u_bin2seven (.bin(d_ff_1_q), .seven({G, F, E, D, C, B, A}));

  assign AN = 8'hfe;
endmodule

/* Code of bin2seven:
module bin2seven (
	input [3:0] bin,
	output reg [6:0] seven);

	always @(bin)
	begin
		case (bin)
		4'h0 : seven = 7'b1000000;
		4'h1 : seven = 7'b1111001;
		4'h2 : seven = 7'b0100100;
		4'h3 : seven = 7'b0110000;
		4'h4 : seven = 7'b0011001;
		4'h5 : seven = 7'b0010010;
		4'h6 : seven = 7'b0000010;
		4'h7 : seven = 7'b1111000;
		4'h8 : seven = 7'b0000000;
		4'h9 : seven = 7'b0010000;
		4'hA : seven = 7'b0001000;
		4'hB : seven = 7'b0000011;
		4'hC : seven = 7'b1000110;
		4'hD : seven = 7'b0100001;
		4'hE : seven = 7'b0000110;
		4'hF : seven = 7'b0001110;
		default : seven = 7'b0000000;
		endcase
	end
endmodule
*/
