// Digital circuit down59n.dig as structural Verilog
module down59n (
  input  CLK,
  input  RESET,
  output [3:0] UNITS,
  output [3:0] TENS
);

  wire downcounter_new_1_zero, units_zero;

  downcounter_new u_units (
    .EN(1'b1), .LOAD(units_zero), .IN(4'b1001), .CLK(CLK), .RESET(RESET), .CNT(UNITS), .ZERO(units_zero));
  downcounter_new downcounter_new_1 (
    .EN(units_zero), .LOAD(downcounter_new_1_zero), .IN(4'b0101), .CLK(CLK), .RESET(RESET), .CNT(TENS),
    .ZERO(downcounter_new_1_zero));
endmodule
