// Digital circuit down59testn.dig as structural Verilog
module down59testn (
  input  clk
);

  wire [3:0] down59n_1_tens, down59n_1_units;

  down59n down59n_1 (.CLK(clk), .RESET(1'b1), .UNITS(down59n_1_units), .TENS(down59n_1_tens));
  Seven_Seg_Hex seven_seg_hex_1 (.d(down59n_1_tens), .dp(1'b0));
  Seven_Seg_Hex seven_seg_hex_2 (.d(down59n_1_units), .dp(1'b0));

  // Notes on the sheet:
  //   clk: Hz: 2
endmodule
