// Digital circuit down59.dig as structural Verilog
module down59 (
  input  CLK,
  output [3:0] UNITS,
  output [3:0] TENS
);

  wire tens_zero, units_zero;

  downcounter u_tens (.EN(units_zero), .LOAD(tens_zero), .IN(4'b0101), .CLK(CLK), .CNT(TENS), .ZERO(tens_zero));
  downcounter u_units (.EN(1'b1), .LOAD(units_zero), .IN(4'b1001), .CLK(CLK), .CNT(UNITS), .ZERO(units_zero));
endmodule
