// Digital circuit down59test.dig as structural Verilog
module down59test (
  input  clk
);

  wire [3:0] down59_1_tens, down59_1_units;

  down59 down59_1 (.CLK(clk), .UNITS(down59_1_units), .TENS(down59_1_tens));
  Seven_Seg_Hex seven_seg_hex_1 (.d(down59_1_tens), .dp(1'b0));
  Seven_Seg_Hex seven_seg_hex_2 (.d(down59_1_units), .dp(1'b0));

  // Notes on the sheet:
  //   clk: Hz: 2
endmodule
