// Digital circuit downcounter.dig as structural Verilog
module downcounter (
  input  EN,
  input  LOAD,
  input  [3:0] IN,
  input  CLK,
  output [3:0] CNT,
  output ZERO
);

  wire and_1_out, and_2_out, and_3_out, multiplexer_1_out, multiplexer_2_out, multiplexer_3_out,
       multiplexer_4_out, t_ff_1_nq, t_ff_2_nq, t_ff_3_nq, t_ff_4_nq;

  and and_1 (and_1_out, t_ff_1_nq, EN);
  and and_2 (and_2_out, t_ff_2_nq, and_1_out);
  and and_3 (and_3_out, t_ff_3_nq, and_2_out);
  and and_4 (ZERO, t_ff_4_nq, and_3_out);
  Multiplexer multiplexer_1 (.sel(LOAD), .in_0(EN), .in_1(IN[0]), .out(multiplexer_1_out));
  Multiplexer multiplexer_2 (.sel(LOAD), .in_0(and_1_out), .in_1(IN[1]), .out(multiplexer_2_out));
  Multiplexer multiplexer_3 (.sel(LOAD), .in_0(and_2_out), .in_1(IN[2]), .out(multiplexer_3_out));
  Multiplexer multiplexer_4 (.sel(LOAD), .in_0(and_3_out), .in_1(IN[3]), .out(multiplexer_4_out));
  T_FF t_ff_1 (.T(multiplexer_1_out), .C(CLK), .Q(CNT[0]), .nQ(t_ff_1_nq));
  T_FF t_ff_2 (.T(multiplexer_2_out), .C(CLK), .Q(CNT[1]), .nQ(t_ff_2_nq));
  T_FF t_ff_3 (.T(multiplexer_3_out), .C(CLK), .Q(CNT[2]), .nQ(t_ff_3_nq));
  T_FF t_ff_4 (.T(multiplexer_4_out), .C(CLK), .Q(CNT[3]), .nQ(t_ff_4_nq));
endmodule
