// Digital circuit eggtimer.dig as structural Verilog
module eggtimer (
  input  _1_kHz
);

  wire PRESET_out, RST_out, START_out, u_controller_countdown, u_controller_load, u_controller_start,
       u_counter_endd, u_downcounter_zero;
  wire [3:0] dipswitch_1_out, dipswitch_5_out, dipswitch_9_out, dipswitch_13_out, u_downcounter_m1,
       u_downcounter_m10, u_downcounter_s1, u_downcounter_s10;

  Button #(.activeLow("true")) RST (.out(RST_out));
  Seven_Seg_Hex seven_seg_hex_1 (.d(u_downcounter_m10), .dp(1'b0));
  DipSwitch dipswitch_1 (.out(dipswitch_1_out[3]));
  DipSwitch dipswitch_2 (.out(dipswitch_1_out[2]));
  DipSwitch dipswitch_3 (.out(dipswitch_1_out[1]));
  Seven_Seg_Hex seven_seg_hex_2 (.d(u_downcounter_m1), .dp(1'b1));
  downcounter #(.applicationType("IVERILOG")) u_downcounter (
    .rst(RST_out), .c1khz(_1_kHz), .count(u_controller_countdown), .load(u_controller_load),
    .pm10(dipswitch_1_out), .pm1(dipswitch_5_out), .ps10(dipswitch_9_out), .ps1(dipswitch_13_out),
    .m10(u_downcounter_m10), .m1(u_downcounter_m1), .s10(u_downcounter_s10), .s1(u_downcounter_s1),
    .zero(u_downcounter_zero));
  DipSwitch dipswitch_4 (.out(dipswitch_1_out[0]));
  DipSwitch dipswitch_5 (.out(dipswitch_5_out[3]));
  DipSwitch dipswitch_6 (.out(dipswitch_5_out[2]));
  Seven_Seg_Hex seven_seg_hex_3 (.d(u_downcounter_s10), .dp(1'b0));
  DipSwitch dipswitch_7 (.out(dipswitch_5_out[1]));
  DipSwitch dipswitch_8 (.out(dipswitch_5_out[0]));
  DipSwitch dipswitch_9 (.out(dipswitch_9_out[3]));
  Seven_Seg_Hex seven_seg_hex_4 (.d(u_downcounter_s1), .dp(1'b0));
  DipSwitch dipswitch_10 (.out(dipswitch_9_out[2]));
  DipSwitch dipswitch_11 (.out(dipswitch_9_out[1]));
  DipSwitch dipswitch_12 (.out(dipswitch_9_out[0]));
  DipSwitch dipswitch_13 (.out(dipswitch_13_out[3]));
  DipSwitch dipswitch_14 (.out(dipswitch_13_out[2]));
  DipSwitch dipswitch_15 (.out(dipswitch_13_out[1]));
  DipSwitch dipswitch_16 (.out(dipswitch_13_out[0]));
  controller #(.applicationType("IVERILOG")) u_controller (
    .clk(_1_kHz), .rst(RST_out), .beginn(START_out), .reset(PRESET_out), .zero(u_downcounter_zero),
    .endd(u_counter_endd), .load(u_controller_load), .start(u_controller_start),
    .countdown(u_controller_countdown));
  Button START (.out(START_out));
  Button PRESET (.out(PRESET_out));
  counter #(.applicationType("IVERILOG")) u_counter (
    .rst(RST_out), .clk(_1_kHz), .start(u_controller_start), .endd(u_counter_endd));

  // Notes on the sheet:
  //   _1_kHz: Hz: 1000
endmodule

/* Code of downcounter:
module downcounter(
    input rst, c1khz,
    input count, load, 
    input [3:0] pm10,
    input [3:0] pm1,
    input [3:0] ps10,
    input [3:0] ps1,
    output reg [3:0] m10,
    output reg [3:0] m1,
    output reg [3:0] s10,
    output reg [3:0] s1,
    output reg zero);

    
    always @(posedge c1khz, posedge load, negedge rst)
    begin
        
        if (load) begin
	    s1 <= ps1;
	    s10 <= ps10;
	    m1 <= pm1;
	    m10 <= pm10;
	end
        
        if (~rst) begin
            s1 <= 0;
            s10 <= 0;
            m1 <= 0;
            m10 <= 0;
        end
        
        if (count)
        begin
	    
	    if (s1 != 0) begin  
	       s1 <= s1-1;
	    end
	    
	    else if (s10 != 0) begin
	        s1 <= 9; 
	        s10 <= s10-1;
	    end
	    
	    else if(m1 != 0) begin
	        s10 <= 5;
		s1 <= 9;
	        m1 <= m1-1;
	    end
	    
	    else if (m10 != 0) begin
	        m1 <= 9;
		s10 <= 5;
		s1 <= 9;
	        m10 <= m10-1;
	    end
	    
	 end // end of = if (count)
         if(m10 == 0 & m1 == 0 & s10 == 0 & s1 == 0) begin
         zero <= 1;
	 end  
         else
         begin
         zero <= 0;
         end
    end // always end
endmodule
*/

/* Code of controller:
module controller
   (
    input clk,
    input rst,
    input beginn, 
    input reset,
    input zero,
    input endd,
    output reg load,
    output reg start,
    output reg countdown
    ); 
    reg thewire = 0;
    reg check = 0;
    
     
    always@(beginn,reset,endd,zero)
    begin 
       
       
       if(zero | ~rst)
       begin
          if(reset)
          begin
             load <= 1;
          end
          else
          begin
             load <= 0;
          end
          countdown <= 0;
          start <= 1;
          assign thewire = 1;
          assign check = 1;
       end
       else
       begin
       countdown <= 0;
       if(reset)
       begin
          load <= 1;
       end
       else
       begin
          load <= 0;
       end 

       if(beginn)
       begin
         if(~start)
         begin
         start <= 1;
         end
         if(check)
         begin
            assign thewire = 0;
         end
       end
    
       if(endd & ~beginn)
          begin
             countdown <= 1;
             start <= 1;
          end
       else if(~endd & ~beginn & ~thewire)
          begin
             start <= 0;
          end
       
       
       end
                    
    end

            
    
    
   
endmodule
*/

/* Code of counter:
module counter(
    input rst,
    input clk,
    input start,
    output endd);
    
    reg [9:0] cnt;
    
    assign endd = (cnt==0);
    
    always @(posedge clk, negedge rst)
    begin
        if (~rst)
        begin
            cnt <= 0;
        end
        else
        begin
            if (start)
                cnt <= 999;
            else if (~endd)
                cnt <= cnt-1;
        end
    end // always
endmodule
*/
